# Fritzing sketch bell_schematic (saved by Fritzing 1.0.1rc)
breadboards: 2

parts:
  U1 = ESP32-38PinWide [part_number=ESP32-38PinWide]
  S1 = Round Pushbutton
  LED2 = smd LED [color="Green (565nm)" package="0805 [SMD]"]
  J1 = Power Jack [package=power_jack_pth_lock]
  XL1 = XL6009 Step-Up module

nets:
  N1: U1.GPIO11, J1.GND, J1.GNDBREAK, XL1.IN-, XL1.OUT-
  N2: U1.VIN, XL1.OUT+
  N3: U1.GPIO15, S1.leg0
  N4: U1.GPIO2, LED2.anode
  N5: S1.leg1, LED2.cathode
  N6: J1.PWR, XL1.IN+

custom parts:
  ESP32-38PinWide: Generic 38-Pin ESP32 with wide format (only access to one side of pins on a breadboard) based on Stephen Lilley's HiLetgo ESP-WROOM-32 ESP32 ESP-32S Development Board.
  XL6009 Step-Up module: XL6009 DC-DC Step UP Power Supply Module --> 5V~35V, 4A.
