# Fritzing sketch gelang_schematic (saved by Fritzing 1.0.1rc)

parts:
  U1 = ESP32-38PinWide [part_number=ESP32-38PinWide]
  A1 = PWM Vibration Motor Switch Toy Sensor Module/Mobile Phone Vibrator (DC 5V)
  TP1 = TP4056 [chip_label=TP4056 package="DIP (Dual Inline) [THT]"]
  Part1 = LIPO-2200mAh
  A2 = PWM Vibration Motor Switch Toy Sensor Module/Mobile Phone Vibrator (DC 5V)  # not connected

nets:
  N1: U1.GPIO11, A1.GND
  VIN: U1.VIN, A1.VCC
  N2: U1.GPIO2, A1.IN
  N3: TP1.pin4, Part1.+
  N4: TP1.pin5, Part1.-

custom parts:
  ESP32-38PinWide: Generic 38-Pin ESP32 with wide format (only access to one side of pins on a breadboard) based on Stephen Lilley's HiLetgo ESP-WROOM-32 ESP32 ESP-32S Development Board.
  TP4056: A DIP stand-in part for whatever IC you want. With 6 pins on a 300mil dual inline package (DIP) footprint.
  LIPO-2200mAh: 2200mAh Lipo-battery
